// Logisim project ax8.circ as structural Verilog: 37 circuits, main circuit toplevel
module toplevel (
);

  wire clock_1_out, IN_HLT, OE, OUT_HLT, RDY, RESET, WE;
  wire [7:0] IN_DATA_BUS, OUT_DATA_BUS, ram_1_data, RAM_DATA, ROM_DATA;
  wire [15:0] ADDR_BUS;

  // DipSwitch #(.number(3)) dipswitch_1: pin names not known; wires that end beside it: IN_HLT, RDY, RESET
  not not_1 (WE, OE);
  mux_2to1_8 mux_2to1_8_1 (.S(ADDR_BUS[15]), .IN0(RAM_DATA), .IN1(ROM_DATA), .Y(IN_DATA_BUS));
  Clock clock_1 (.out(clock_1_out));
  RAM #(.addrWidth(15), .databus("bidir"), .enables("line"), .trigger("low")) ram_1 (
    .addr(ADDR_BUS[14:0]), .we(WE), .oe(OE), .clk(ADDR_BUS[15]), .data(ram_1_data));
  ROM #(.addrWidth(15)) rom_1 (.addr(ADDR_BUS[14:0]), .data(ROM_DATA));
  cpu cpu_1 (
    .RST_N(RESET), .RDY(RDY), .IN_HLT(IN_HLT), .IN_DATA_BUS(IN_DATA_BUS), .CLK(clock_1_out), .RW(OE),
    .ADDR_BUS(ADDR_BUS), .OUT_DATA_BUS(OUT_DATA_BUS), .OUT_HLT(OUT_HLT));
  assign RAM_DATA = OE ? ram_1_data : 8'bz;  // Controlled_Buffer controlled_buffer_1
  assign ram_1_data = WE ? OUT_DATA_BUS : 8'bz;  // Controlled_Buffer controlled_buffer_2

  // Other names for the same wires on the sheet: DECODED_ADDR[14:0] = ADDR_BUS[14:0]; SEL_ROM = ADDR_BUS[15]; RW = OE

  // Notes on the sheet:
  //   contents of rom_1 (hex, n*v repeats v):
  //   91 10 80 1f 12*0 57 42 50 38 24 ff 1 1f 32729*0 80
endmodule

module cpu (
  input  CLK,
  input  RST_N,
  input  RDY,
  input  IN_HLT,
  input  [7:0] IN_DATA_BUS,
  output OUT_HLT,
  output RW,
  output [15:0] ADDR_BUS,
  output [7:0] OUT_DATA_BUS
);

  wire ALU_DL_WE, ALU_HLT, ALU_WB, ALU_WRITE, and_1_out, and_4_out, CLK_t, COMMIT, d_flipflop_2_q, DEC_HLT,
       DEC_RW, DL_WE, HLT, INT_DONE, INT_MEM_RW, INT_OP_HI_WE, INT_OP_LO_WE, IR_WE, not_1_out, OP_HI_WE,
       OP_LO_WE, or_1_out, OUT_RST, RST_REQ, SEQ_DL_WE, SEQ_ENABLE, SEQ_MEM_RW, SEQ_OP_HI_WE, SEQ_OP_LO_WE,
       WE_A, WE_IX, WE_IY;
  wire [1:0] ADDR_SEL, DEC_MODE, DEC_PC_OP, DST_SEL, INT_ADDR_SEL, INT_PC_OP, mux_2to1_2_2_y, PC_OP,
       SEQ_ADDR_SEL, SEQ_PC_OP;
  wire [2:0] SRC_SEL;
  wire [3:0] ALU_FR_DATA, ALU_FR_WE, ALU_OP, DEC_FR_DATA, DEC_FR_WE, FR_DATA, FR_Q, FR_WE, INT_FR_DATA,
       INT_FR_WE, mux_2to1_4_1_y, mux_2to1_4_2_y, VEC_LO;
  wire [7:0] A_Q, ALU_A, ALU_B, ALU_Y, DL_DATA, DL_Q, HI_PC, IR_Q, IX_Q, IY_Q, LO_PC, OP_HI_Q, OP_LO_Q;

  Register #(.trigger("high")) A (.D(A_Q), .en(1'b1), .clk(1'b1));  // open: Q, clr
  Register #(.trigger("high")) IX (.D(IX_Q), .en(1'b1), .clk(1'b1));  // open: Q, clr
  Register #(.trigger("high")) IY (.D(IY_Q), .en(1'b1), .clk(1'b1));  // open: Q, clr
  Register #(.trigger("high"), .width(4)) FR (.D(FR_Q), .en(1'b1), .clk(1'b1));  // open: Q, clr
  Register #(.trigger("high"), .width(16)) PC (.D({HI_PC, LO_PC}), .en(1'b1), .clk(1'b1));  // open: Q, clr
  Register #(.trigger("high")) DL (.D(DL_Q), .en(1'b1), .clk(1'b1));  // open: Q, clr
  Register #(.trigger("high")) IR (.D(IR_Q), .en(1'b1), .clk(1'b1));  // open: Q, clr
  Register #(.trigger("high"), .width(16)) OP (.D({OP_HI_Q, OP_LO_Q}), .en(1'b1), .clk(1'b1));  // open: Q, clr
  and and_1 (and_1_out, COMMIT, HLT);
  mux_4to1_8 mux_4to1_8_1 (
    .I0(LO_PC), .I1(OP_LO_Q), .I2(IY_Q), .I3({4'b1111, VEC_LO}), .S(ADDR_SEL), .Y(ADDR_BUS[7:0]));
  mux_4to1_8 mux_4to1_8_2 (.I0(HI_PC), .I1(OP_HI_Q), .I2({8{1'b0}}), .I3({8{1'b1}}), .S(ADDR_SEL), .Y(ADDR_BUS[15:8]));
  mux_2to1_8 mux_2to1_8_1 (.S(ALU_WRITE), .IN0(IN_DATA_BUS), .IN1(ALU_Y), .Y(DL_DATA));
  or or_1 (or_1_out, and_1_out, OUT_HLT, IN_HLT);
  not not_1 (not_1_out, RW);
  d_flipflop d_flipflop_1 (.D(or_1_out), .CLK(CLK_t), .RST(RST_REQ), .Q(OUT_HLT));  // open: NQ
  and and_2 (RST_REQ, ~RST_N, d_flipflop_2_q);  // AND_Gate
  d_flipflop d_flipflop_2 (.D(RST_N), .CLK(CLK), .Q(d_flipflop_2_q));  // open: RST, NQ
  and and_3 (CLK_t, CLK, RDY, ~OUT_HLT);  // AND_Gate
  assign OUT_DATA_BUS = not_1_out ? DL_Q : 8'bz;  // Controlled_Buffer controlled_buffer_1
  register_8 DATA_LATCH (.CLK(CLK_t), .WE(DL_WE), .D(DL_DATA), .Q(DL_Q));  // open: RESET
  register_8 REG_IR (.CLK(CLK_t), .WE(IR_WE), .D(DL_DATA), .RESET(RST_REQ), .Q(IR_Q));
  register_8 REG_OP_LO (.CLK(CLK_t), .WE(OP_LO_WE), .D(DL_DATA), .Q(OP_LO_Q));  // open: RESET
  register_8 REG_OP_HI (.CLK(CLK_t), .WE(OP_HI_WE), .D(DL_DATA), .RESET(RST_REQ), .Q(OP_HI_Q));
  register_8 REG_A (.CLK(CLK_t), .WE(WE_A), .D(ALU_Y), .Q(A_Q));  // open: RESET
  register_8 REG_IX (.CLK(CLK_t), .WE(WE_IX), .D(ALU_Y), .Q(IX_Q));  // open: RESET
  register_8 REG_IY (.CLK(CLK_t), .WE(WE_IY), .D(ALU_Y), .Q(IY_Q));  // open: RESET
  program_counter REG_PC (.OP(PC_OP), .DATA({OP_HI_Q, OP_LO_Q}), .CLK(CLK_t), .PC({HI_PC, LO_PC}));
  flag_register REG_FR (.FR_DATA(FR_DATA), .FR_WE(FR_WE), .CLK(CLK_t), .FR_Q(FR_Q));
  and and_4 (and_4_out, ~OUT_HLT, INT_DONE);  // AND_Gate
  alu alu_1 (
    .A(ALU_A), .B(ALU_B), .Cin(FR_Q[3]), .Vin(FR_Q[2]), .OP(ALU_OP), .Y(ALU_Y), .FR_DATA(ALU_FR_DATA),
    .FR_WE(ALU_FR_WE), .HALT(ALU_HLT));
  mux_4to1_8 mux_4to1_8_3 (.I0(A_Q), .I1(IX_Q), .I2(IY_Q), .I3(DL_Q), .S(DST_SEL), .Y(ALU_A));
  and and_5 (ALU_WRITE, COMMIT, ALU_WB);
  interrupt_sequencer interrupt_sequencer_1 (
    .CLK(CLK_t), .RESET(RST_REQ), .DONE(INT_DONE), .OUT_RST(OUT_RST), .MEM_RW(INT_MEM_RW),
    .OP_LO_WE(INT_OP_LO_WE), .OP_HI_WE(INT_OP_HI_WE), .ADDR_SEL(INT_ADDR_SEL), .PC_OP(INT_PC_OP),
    .FR_WE(INT_FR_WE), .FR_DATA(INT_FR_DATA), .VEC(VEC_LO));
  d_flipflop d_flipflop_3 (.D(and_4_out), .CLK(CLK_t), .Q(SEQ_ENABLE));  // open: RST, NQ
  instruction_sequencer instruction_sequencer_1 (
    .CLK(CLK_t), .RESET(OUT_RST), .ENABLE(SEQ_ENABLE), .RW(DEC_RW), .PC_OP_IN(DEC_PC_OP), .MODE(DEC_MODE),
    .COMMIT(COMMIT), .MEM_RW(SEQ_MEM_RW), .DL_WE(SEQ_DL_WE), .IR_WE(IR_WE), .OP_LO_WE(SEQ_OP_LO_WE),
    .OP_HI_WE(SEQ_OP_HI_WE), .ADDR_SEL(SEQ_ADDR_SEL), .PC_OP(SEQ_PC_OP));
  mux_8to1_8 mux_8to1_8_1 (
    .IN7({8{1'b1}}), .IN6({8{1'b0}}), .IN5({8{1'b1}}), .IN4({8{1'b0}}), .IN3(DL_Q), .IN2(IY_Q), .IN1(IX_Q),
    .IN0(A_Q), .S(SRC_SEL), .out_10(ALU_B));
  demux_4to1 demux_4to1_1 (.I(ALU_WRITE), .S(DST_SEL), .Y0(WE_A), .Y1(WE_IX), .Y2(WE_IY), .Y3(ALU_DL_WE));
  or or_2 (HLT, IN_HLT, DEC_HLT, ALU_HLT);
  or or_3 (DL_WE, SEQ_DL_WE, ALU_DL_WE);
  mux_2to1 mux_2to1_1 (.IN0(INT_MEM_RW), .IN1(SEQ_MEM_RW), .S(INT_DONE), .Y(RW));
  mux_2to1 mux_2to1_2 (.IN0(INT_OP_LO_WE), .IN1(SEQ_OP_LO_WE), .S(INT_DONE), .Y(OP_LO_WE));
  mux_2to1 mux_2to1_3 (.IN0(INT_OP_HI_WE), .IN1(SEQ_OP_HI_WE), .S(INT_DONE), .Y(OP_HI_WE));
  mux_2to1_2 mux_2to1_2_1 (.S(INT_DONE), .IN0(INT_ADDR_SEL), .IN1(SEQ_ADDR_SEL), .Y(ADDR_SEL));
  instruction_decoder instruction_decoder_1 (
    .FR(FR_Q), .IR(IR_Q), .HLT(DEC_HLT), .RW(DEC_RW), .ALU_WB(ALU_WB), .PC_OP(DEC_PC_OP), .MODE(DEC_MODE),
    .DST_SEL(DST_SEL), .SRC_SEL(SRC_SEL), .FR_WE(DEC_FR_WE), .FR_DATA(DEC_FR_DATA), .ALU_OP(ALU_OP));
  mux_2to1_4 mux_2to1_4_1 (.S(INT_DONE), .IN0(INT_FR_WE), .IN1(DEC_FR_WE), .Y(mux_2to1_4_1_y));
  mux_2to1_4 mux_2to1_4_2 (.S(INT_DONE), .IN0(INT_FR_DATA), .IN1(DEC_FR_DATA), .Y(mux_2to1_4_2_y));
  mux_2to1_2 mux_2to1_2_2 (.S(INT_DONE), .IN0(INT_PC_OP), .IN1(SEQ_PC_OP), .Y(mux_2to1_2_2_y));
  mux_2to1_4 mux_2to1_4_3 (.S(ALU_WRITE), .IN0(mux_2to1_4_1_y), .IN1(ALU_FR_WE), .Y(FR_WE));
  mux_2to1_4 mux_2to1_4_4 (.S(ALU_WRITE), .IN0(mux_2to1_4_2_y), .IN1(ALU_FR_DATA), .Y(FR_DATA));
  mux_2to1_2 mux_2to1_2_3 (.S(COMMIT), .IN0(mux_2to1_2_2_y), .IN1(DEC_PC_OP), .Y(PC_OP));

  // Other names for the same wires on the sheet: LO_ADDR_BUS[7:0] = ADDR_BUS[7:0]; HI_ADDR_BUS[7:0] = ADDR_BUS[15:8];
  //   HALTED = OUT_HLT; IN_CLK = CLK; IN_RST_N = RST_N; MEM_RW = RW

  // Notes on the sheet:
  //   PROBING ENVIRONMENT
  //   IO INTERFACING
  //   REGISTERS SECTION
  //   TIMING SECTION
  //   ALU EXECUTION
  //   <= DELAY SEQUENCER ENABLING
  //   DECODING SECTION
endmodule

module interrupt_sequencer (
  input  CLK,
  input  RESET,
  output DONE,
  output OUT_RST,
  output MEM_RW,
  output OP_LO_WE,
  output OP_HI_WE,
  output [1:0] ADDR_SEL,
  output [1:0] PC_OP,
  output [3:0] FR_WE,
  output [3:0] FR_DATA,
  output [3:0] VEC
);

  wire D0, D1, not_1_out, nQ0, or_1_out, or_2_out, Q0, Q1;

  d_flipflop d_flipflop_1 (.D(D0), .CLK(CLK), .RST(RESET), .Q(Q0), .NQ(nQ0));
  d_flipflop d_flipflop_2 (.D(D1), .CLK(CLK), .RST(RESET), .Q(Q1), .NQ(ADDR_SEL[1]));
  demux_4to1 demux_4to1_1 (.I(1'b1), .S({Q1, Q0}), .Y0(OP_LO_WE), .Y1(OP_HI_WE), .Y2(FR_WE[3]), .Y3(DONE));
  not not_1 (not_1_out, RESET);
  and and_1 (D0, not_1_out, or_1_out);
  or or_1 (or_1_out, nQ0, Q1);
  and and_2 (D1, not_1_out, or_2_out);
  or or_2 (or_2_out, Q0, Q1);

  assign ADDR_SEL[0] = ADDR_SEL[1];
  assign FR_DATA = 4'b0000;
  assign FR_WE[2:0] = {3{FR_WE[3]}};
  assign MEM_RW = 1'b1;
  assign OUT_RST = FR_WE[3];
  assign PC_OP = {FR_WE[3], 1'b0};
  assign VEC = {3'b000, OP_HI_WE};

  // Other names for the same wires on the sheet: nQ1 = ADDR_SEL[1]; REa = FR_WE[3]; R0a = OP_LO_WE; REb = DONE;
  //   RST = RESET; R0b = OP_HI_WE
endmodule

module instruction_sequencer (
  input  CLK,
  input  RESET,
  input  ENABLE,
  input  RW,
  input  [1:0] PC_OP_IN,
  input  [1:0] MODE,
  output COMMIT,
  output MEM_RW,
  output DL_WE,
  output IR_WE,
  output OP_LO_WE,
  output OP_HI_WE,
  output [1:0] ADDR_SEL,
  output [1:0] PC_OP
);

  wire and_1_out, and_14_out, and_15_out, and_16_out, and_17_out, and_18_out, and_19_out, and_20_out,
       and_21_out, and_22_out, d_flipflop_1_nq, d_flipflop_2_nq, d_flipflop_3_nq, d_flipflop_4_nq,
       d_flipflop_5_nq, d_flipflop_6_nq, EX, EXb, EXN, F0, F0b, F1, F1b, F1N, F2, F2b, F2N, F3, F3a, F3N,
       IS_ABS, IS_IMM, IS_IMP, IS_IND, mux_2to1_1_y, mux_2to1_2_y, nPH, or_1_out, or_5_out, or_6_out,
       or_8_out, or_10_out, PH, PHN, RST_REQ, WR;

  and and_1 (and_1_out, CLK, ENABLE);
  demux_4to1 demux_4to1_1 (.I(ENABLE), .S(MODE), .Y0(IS_IMP), .Y1(IS_IND), .Y2(IS_IMM), .Y3(IS_ABS));
  d_flipflop d_flipflop_1 (.D(PHN), .CLK(and_1_out), .RST(RST_REQ), .Q(PH), .NQ(d_flipflop_1_nq));
  // NoConnect on d_flipflop_1_nq
  d_flipflop d_flipflop_2 (.D(F1N), .CLK(and_1_out), .RST(RST_REQ), .Q(F1), .NQ(d_flipflop_2_nq));
  // NoConnect on d_flipflop_2_nq
  d_flipflop d_flipflop_3 (.D(F2N), .CLK(and_1_out), .RST(RST_REQ), .Q(F2), .NQ(d_flipflop_3_nq));
  // NoConnect on d_flipflop_3_nq
  d_flipflop d_flipflop_4 (.D(F3N), .CLK(and_1_out), .RST(RST_REQ), .Q(F3), .NQ(d_flipflop_4_nq));
  // NoConnect on d_flipflop_4_nq
  d_flipflop d_flipflop_5 (.D(EXN), .CLK(and_1_out), .RST(RST_REQ), .Q(EX), .NQ(d_flipflop_5_nq));
  // NoConnect on d_flipflop_5_nq
  not not_1 (WR, RW);
  or or_1 (or_1_out, F3a, EXb);
  and and_2 (RST_REQ, RESET, d_flipflop_6_nq);
  d_flipflop d_flipflop_6 (.D(RESET), .CLK(CLK), .NQ(d_flipflop_6_nq));  // open: RST, Q
  not not_2 (nPH, PH);
  and and_3 (IR_WE, ~PH, F0);  // AND_Gate
  and and_4 (F0b, PH, F0);
  and and_5 (OP_LO_WE, ~PH, F1);  // AND_Gate
  and and_6 (F1b, PH, F1);
  and and_7 (OP_HI_WE, ~PH, F2);  // AND_Gate
  and and_8 (F2b, PH, F2);
  and and_9 (F3a, ~PH, F3);  // AND_Gate
  and and_10 (COMMIT, ~PH, EX);  // AND_Gate
  and and_11 (EXb, PH, EX);
  not not_3 (MEM_RW, EXb);
  or or_2 (DL_WE, OP_LO_WE, OP_HI_WE, F3a);
  and and_12 (ADDR_SEL[0], IS_ABS, or_1_out);
  and and_13 (ADDR_SEL[1], IS_IND, or_1_out);
  nor nor_1 (F0, F1, F2, F3, EX);
  nor nor_2 (PHN, PH, F3a, and_14_out);
  and and_14 (and_14_out, EX, RW);
  or or_3 (F1N, OP_LO_WE, and_15_out);
  and and_15 (and_15_out, F0b, MODE[1]);
  or or_4 (F2N, OP_HI_WE, and_16_out);
  and and_16 (and_16_out, F1b, IS_ABS);
  mux_2to1 mux_2to1_1 (.IN0(1'b0), .IN1(PC_OP_IN[0]), .S(COMMIT), .Y(mux_2to1_1_y));
  mux_2to1 mux_2to1_2 (.IN0(1'b0), .IN1(PC_OP_IN[1]), .S(COMMIT), .Y(mux_2to1_2_y));
  or or_5 (or_5_out, F0b, F1b, F2b);
  and and_17 (and_17_out, F2b, RW);
  and and_18 (and_18_out, F0b, IS_IND, RW);
  or or_6 (or_6_out, COMMIT, F2b);
  and and_19 (and_19_out, F0b, IS_IND);
  and and_20 (and_20_out, F1b, IS_IMM);
  and and_21 (and_21_out, F0b, IS_IMP);
  mux_2to1 mux_2to1_3 (.IN0(mux_2to1_1_y), .IN1(1'b1), .S(or_5_out), .Y(PC_OP[0]));
  mux_2to1 mux_2to1_4 (.IN0(mux_2to1_2_y), .IN1(1'b1), .S(or_5_out), .Y(PC_OP[1]));
  or or_7 (F3N, and_17_out, and_18_out);
  and and_22 (and_22_out, WR, or_8_out);
  or or_8 (or_8_out, or_6_out, and_19_out);
  or or_9 (EXN, and_22_out, or_10_out);
  or or_10 (or_10_out, F3a, and_20_out, and_21_out);

  // Other names for the same wires on the sheet: M0 = MODE[0]; M1 = MODE[1]; EXa = COMMIT; F0a = IR_WE;
  //   F1a = OP_LO_WE; F2a = OP_HI_WE; RE = RW; RST = RESET

  // Notes on the sheet:
  //   State Machine:
  //   State Decoder:
endmodule

module alu (
  input  [7:0] A,
  input  [7:0] B,
  input  Cin,
  input  Vin,
  input  [3:0] OP,
  output [7:0] Y,
  output [3:0] FR_DATA,
  output [3:0] FR_WE,
  output HALT
);

  wire AdderC, AdderV, MulV, mux_8to1_1_out_10, mux_8to1_2_out_10, or_2_out, ShiftC;
  wire [7:0] AdderY, AndY, MulY, mux_8to1_8_1_out_10, OrY, ShiftY, XorY;

  adder_subtractor adder_subtractor_1 (
    .M(OP[0]), .B(B), .A(A), .Cin(Cin), .Y(AdderY), .Cout(AdderC), .Overflow(AdderV));
  multiplier_4 multiplier_4_1 (.B(B[3:0]), .A(A[3:0]), .Y(MulY), .Overflow(MulV));
  assign AndY = A & B;  // AND_Gate and_1, 8 bits wide
  assign OrY = A | B;  // OR_Gate or_1, 8 bits wide
  assign XorY = A ^ B;  // XOR_Gate xor_1, 8 bits wide
  shifter_8 shifter_8_1 (.A(A), .Cin(Cin), .M(OP[0]), .Y(ShiftY), .Cout(ShiftC));
  mux_8to1_8 mux_8to1_8_1 (
    .IN7(ShiftY), .IN6(ShiftY), .IN5(XorY), .IN4(OrY), .IN3(AndY), .IN2(MulY), .IN1(AdderY), .IN0(AdderY),
    .S(OP[2:0]), .out_10(mux_8to1_8_1_out_10));
  mux_8to1 mux_8to1_1 (
    .S(OP[2:0]), .I0(AdderC), .I1(AdderC), .I2(1'b0), .I3(Cin), .I4(Cin), .I5(Cin), .I6(ShiftC), .I7(ShiftC),
    .out_10(mux_8to1_1_out_10));
  mux_8to1 mux_8to1_2 (
    .S(OP[2:0]), .I0(AdderV), .I1(AdderV), .I2(MulV), .I3(Vin), .I4(Vin), .I5(Vin), .I6(Vin), .I7(Vin),
    .out_10(mux_8to1_2_out_10));
  mux_2to1_8 mux_2to1_8_1 (.S(OP[3]), .IN0(mux_8to1_8_1_out_10), .IN1(B), .Y({FR_DATA[1], Y[6:0]}));
  mux_2to1 mux_2to1_1 (.IN0(mux_8to1_1_out_10), .IN1(Cin), .S(OP[3]), .Y(FR_DATA[2]));
  mux_2to1 mux_2to1_2 (.IN0(mux_8to1_2_out_10), .IN1(Vin), .S(OP[3]), .Y(FR_DATA[3]));
  nor nor_1 (FR_DATA[0], Y[0], Y[1], Y[2], Y[3], Y[4], Y[5], Y[6], FR_DATA[1]);
  or or_2 (or_2_out, OP[0], OP[1], OP[2]);
  and and_2 (HALT, or_2_out, OP[3]);

  assign FR_WE = 4'b1111;
  assign Y[7] = FR_DATA[1];

  // Other names for the same wires on the sheet: ALU_Y[7:0] = {FR_DATA[1], Y[6:0]}; OutZ = FR_DATA[0];
  //   OutN = FR_DATA[1]; OutC = FR_DATA[2]; OutV = FR_DATA[3]; Mov[7:0] = B

  // Notes on the sheet:
  //   Execution =>
  //   Decoder =>
  //   HALT Signal generator
  //   <= Flags output
endmodule

module program_counter (
  input  [1:0] OP,
  input  [15:0] DATA,
  input  CLK,
  output [15:0] PC
);

  wire CIN, IS_JMP, ripple_adder_8_1_c6, ripple_adder_8_1_cout, ripple_adder_8_2_c6, ripple_adder_8_2_cout,
       WE;
  wire [7:0] BRA_PC_HI, BRA_PC_LO, OUT_HI_PC, OUT_LO_PC, Y_PC_HI, Y_PC_LO;
  wire [7:7] xor_1_out;

  xor xor_1 (xor_1_out[7], OP[0], OP[1]);
  and and_1 (IS_JMP, ~OP[0], OP[1]);  // AND_Gate
  and and_2 (CIN, OP[0], OP[1]);
  or or_1 (WE, OP[0], OP[1]);
  ripple_adder_8 ripple_adder_8_1 (
    .A(PC[7:0]), .B(BRA_PC_LO), .Cin(CIN), .Y(Y_PC_LO), .Cout(ripple_adder_8_1_cout), .C6(ripple_adder_8_1_c6));
  // NoConnect on ripple_adder_8_1_c6
  ripple_adder_8 ripple_adder_8_2 (
    .A(PC[15:8]), .B(BRA_PC_HI), .Cin(ripple_adder_8_1_cout), .Y(Y_PC_HI), .Cout(ripple_adder_8_2_cout),
    .C6(ripple_adder_8_2_c6));
  // NoConnect on ripple_adder_8_2_c6
  // NoConnect on ripple_adder_8_2_cout
  assign BRA_PC_LO = DATA[7:0] & {8{xor_1_out[7]}};  // AND_Gate and_3, 8 bits wide
  assign BRA_PC_HI = DATA[15:8] & {8{xor_1_out[7]}};  // AND_Gate and_4, 8 bits wide
  mux_2to1_8 mux_2to1_8_1 (.S(IS_JMP), .IN0(Y_PC_LO), .IN1(DATA[7:0]), .Y(OUT_LO_PC));
  mux_2to1_8 mux_2to1_8_2 (.S(IS_JMP), .IN0(Y_PC_HI), .IN1(DATA[15:8]), .Y(OUT_HI_PC));
  register_8 register_8_1 (.CLK(CLK), .WE(WE), .D(OUT_LO_PC), .Q(PC[7:0]));  // open: RESET
  register_8 register_8_2 (.CLK(CLK), .WE(WE), .D(OUT_HI_PC), .Q(PC[15:8]));  // open: RESET

  // Other names for the same wires on the sheet: LO_DATA[7:0] = DATA[7:0]; HI_DATA[7:0] = DATA[15:8];
  //   LO_PC[7:0] = PC[7:0]; HI_PC[7:0] = PC[15:8]

  // Notes on the sheet:
  //   DECODE OPERATION =>
endmodule

module flag_register (
  input  [3:0] FR_DATA,
  input  [3:0] FR_WE,
  input  CLK,
  output [3:0] FR_Q
);

  wire mux_2to1_1_y, mux_2to1_2_y, mux_2to1_3_y, mux_2to1_4_y, undriven, undriven_2, undriven_3, undriven_4;

  mux_2to1 mux_2to1_1 (.IN0(FR_Q[0]), .IN1(FR_DATA[0]), .S(FR_WE[0]), .Y(mux_2to1_1_y));
  mux_2to1 mux_2to1_2 (.IN0(FR_Q[1]), .IN1(FR_DATA[1]), .S(FR_WE[1]), .Y(mux_2to1_2_y));
  mux_2to1 mux_2to1_3 (.IN0(FR_Q[2]), .IN1(FR_DATA[2]), .S(FR_WE[2]), .Y(mux_2to1_3_y));
  mux_2to1 mux_2to1_4 (.IN0(FR_Q[3]), .IN1(FR_DATA[3]), .S(FR_WE[3]), .Y(mux_2to1_4_y));
  // NoConnect on undriven
  // NoConnect on undriven_2
  // NoConnect on undriven_3
  // NoConnect on undriven_4
  d_flipflop d_flipflop_1 (.D(mux_2to1_1_y), .CLK(CLK), .RST(undriven), .Q(FR_Q[0]));  // open: NQ
  d_flipflop d_flipflop_2 (.D(mux_2to1_2_y), .CLK(CLK), .RST(undriven_2), .Q(FR_Q[1]));  // open: NQ
  d_flipflop d_flipflop_3 (.D(mux_2to1_3_y), .CLK(CLK), .RST(undriven_3), .Q(FR_Q[2]));  // open: NQ
  d_flipflop d_flipflop_4 (.D(mux_2to1_4_y), .CLK(CLK), .RST(undriven_4), .Q(FR_Q[3]));  // open: NQ

  // Other names for the same wires on the sheet: FR_Z = FR_DATA[0]; FR_N = FR_DATA[1]; FR_C = FR_DATA[2];
  //   FR_V = FR_DATA[3]; OUT_Z = FR_Q[0]; OUT_N = FR_Q[1]; OUT_C = FR_Q[2]; OUT_V = FR_Q[3]; WE_Z = FR_WE[0];
  //   WE_N = FR_WE[1]; WE_C = FR_WE[2]; WE_V = FR_WE[3]
endmodule

module register_8 (
  input  CLK,
  input  WE,
  input  [7:0] D,
  input  RESET,
  output [7:0] Q
);

  register_4 register_4_1 (.RESET(RESET), .CLK(CLK), .WE(WE), .D(D[3:0]), .Q(Q[3:0]));
  register_4 register_4_2 (.RESET(RESET), .CLK(CLK), .WE(WE), .D(D[7:4]), .Q(Q[7:4]));

  // Other names for the same wires on the sheet: D_LO[3:0] = D[3:0]; D_HI[3:0] = D[7:4]; Q_LO[3:0] = Q[3:0];
  //   Q_HI[3:0] = Q[7:4]
endmodule

module register_4 (
  input  CLK,
  input  WE,
  input  [3:0] D,
  input  RESET,
  output [3:0] Q
);

  wire d_flipflop_1_nq, d_flipflop_2_nq, d_flipflop_3_nq, d_flipflop_4_nq, mux_2to1_1_y, mux_2to1_2_y,
       mux_2to1_3_y, mux_2to1_4_y;

  mux_2to1 mux_2to1_1 (.IN0(Q[0]), .IN1(D[0]), .S(WE), .Y(mux_2to1_1_y));
  mux_2to1 mux_2to1_2 (.IN0(Q[1]), .IN1(D[1]), .S(WE), .Y(mux_2to1_2_y));
  mux_2to1 mux_2to1_3 (.IN0(Q[2]), .IN1(D[2]), .S(WE), .Y(mux_2to1_3_y));
  mux_2to1 mux_2to1_4 (.IN0(Q[3]), .IN1(D[3]), .S(WE), .Y(mux_2to1_4_y));
  d_flipflop d_flipflop_1 (.D(mux_2to1_1_y), .CLK(CLK), .RST(RESET), .Q(Q[0]), .NQ(d_flipflop_1_nq));
  // NoConnect on d_flipflop_1_nq
  d_flipflop d_flipflop_2 (.D(mux_2to1_2_y), .CLK(CLK), .RST(RESET), .Q(Q[1]), .NQ(d_flipflop_2_nq));
  // NoConnect on d_flipflop_2_nq
  d_flipflop d_flipflop_3 (.D(mux_2to1_3_y), .CLK(CLK), .RST(RESET), .Q(Q[2]), .NQ(d_flipflop_3_nq));
  // NoConnect on d_flipflop_3_nq
  d_flipflop d_flipflop_4 (.D(mux_2to1_4_y), .CLK(CLK), .RST(RESET), .Q(Q[3]), .NQ(d_flipflop_4_nq));
  // NoConnect on d_flipflop_4_nq
endmodule

module instruction_decoder (
  input  [3:0] FR,
  input  [7:0] IR,
  output HLT,
  output RW,
  output ALU_WB,
  output [1:0] PC_OP,
  output [1:0] MODE,
  output [1:0] DST_SEL,
  output [2:0] SRC_SEL,
  output [3:0] FR_WE,
  output [3:0] FR_DATA,
  output [3:0] ALU_OP
);

  wire ALU_WB_t, and_1_out, ARI_ALU_WB, ARI_HLT, demux_2to1_1_y0, G_ARI, G_JMP, G_MEM, G_SYS, G_UNY, JMP_HLT,
       MEM_ALU_WB, MEM_HLT, MEM_RW, or_1_out, or_2_out, SYS_HLT, UNY_ALU_WB, UNY_HLT;
  wire [1:0] ARI_DST_SEL, ARI_MODE, DST_SEL_t, JMP_MODE, JMP_PC_OP, MEM_DST_SEL, MEM_MODE, MODE_t,
       UNY_DST_SEL, UNY_MODE;
  wire [1:1] not_1_out;
  wire [2:0] ARI_SRC_SEL, MEM_SRC_SEL, SRC_SEL_t, UNY_SRC_SEL;
  wire [3:0] ALU_OP_t, ARI_ALU_OP, FR_DATA_t, FR_WE_t, MEM_ALU_OP, SYS_FR_DATA, SYS_FR_WE, UNY_ALU_OP,
       UNY_FR_DATA, UNY_FR_WE;

  demux_2to1 demux_2to1_1 (.S(IR[7]), .I(1'b1), .Y0(demux_2to1_1_y0), .Y1(G_JMP));
  demux_4to1 demux_4to1_1 (.I(demux_2to1_1_y0), .S(IR[6:5]), .Y0(G_SYS), .Y1(G_MEM), .Y2(G_ARI), .Y3(G_UNY));
  decode_system decode_system_1 (.E(G_SYS), .FR(FR), .IR(IR), .HLT(SYS_HLT), .FR_WE(SYS_FR_WE), .FR_DATA(SYS_FR_DATA));
  decode_memory decode_memory_1 (
    .E(G_MEM), .FR(FR), .IR(IR), .HLT(MEM_HLT), .MEM_RW(MEM_RW), .ALU_WB(MEM_ALU_WB), .MODE(MEM_MODE),
    .DST_SEL(MEM_DST_SEL), .SRC_SEL(MEM_SRC_SEL), .ALU_OP(MEM_ALU_OP));
  decode_arithmetic decode_arithmetic_1 (
    .E(G_ARI), .FR(FR), .IR(IR), .HLT(ARI_HLT), .ALU_WB(ARI_ALU_WB), .MODE(ARI_MODE), .DST_SEL(ARI_DST_SEL),
    .SRC_SEL(ARI_SRC_SEL), .ALU_OP(ARI_ALU_OP));
  decode_unary decode_unary_1 (
    .E(G_UNY), .FR(FR), .IR(IR), .HLT(UNY_HLT), .ALU_WB(UNY_ALU_WB), .MODE(UNY_MODE), .DST_SEL(UNY_DST_SEL),
    .SRC_SEL(UNY_SRC_SEL), .FR_WE(UNY_FR_WE), .FR_DATA(UNY_FR_DATA), .ALU_OP(UNY_ALU_OP));
  decode_jump decode_jump_1 (.E(G_JMP), .FR(FR), .IR(IR), .HLT(JMP_HLT), .MODE(JMP_MODE), .PC_OP(JMP_PC_OP));
  or or_1 (or_1_out, IR[5], IR[6]);
  and and_1 (and_1_out, or_1_out, IR[7]);
  or or_2 (or_2_out, SYS_HLT, MEM_HLT, ARI_HLT, UNY_HLT, JMP_HLT);
  or or_3 (HLT, and_1_out, or_2_out);
  or or_4 (RW, ~G_MEM, MEM_RW);  // OR_Gate
  or or_5 (ALU_WB_t, MEM_ALU_WB, ARI_ALU_WB, UNY_ALU_WB);
  assign MODE_t = MEM_MODE | ARI_MODE | UNY_MODE | JMP_MODE;  // OR_Gate or_6, 2 bits wide
  assign DST_SEL_t = MEM_DST_SEL | ARI_DST_SEL | UNY_DST_SEL;  // OR_Gate or_7, 2 bits wide
  assign SRC_SEL_t = MEM_SRC_SEL | ARI_SRC_SEL | UNY_SRC_SEL;  // OR_Gate or_8, 3 bits wide
  assign FR_WE_t = SYS_FR_WE | UNY_FR_WE;  // OR_Gate or_9, 4 bits wide
  assign FR_DATA_t = SYS_FR_DATA | UNY_FR_DATA;  // OR_Gate or_10, 4 bits wide
  assign ALU_OP_t = MEM_ALU_OP | ARI_ALU_OP | UNY_ALU_OP;  // OR_Gate or_11, 4 bits wide
  not not_1 (not_1_out[1], HLT);
  and and_2 (ALU_WB, not_1_out[1], ALU_WB_t);
  assign PC_OP = {2{not_1_out[1]}} & JMP_PC_OP;  // AND_Gate and_3, 2 bits wide
  assign MODE = {2{not_1_out[1]}} & MODE_t;  // AND_Gate and_4, 2 bits wide
  assign DST_SEL = {2{not_1_out[1]}} & DST_SEL_t;  // AND_Gate and_5, 2 bits wide
  assign SRC_SEL = {3{not_1_out[1]}} & SRC_SEL_t;  // AND_Gate and_6, 3 bits wide
  assign FR_WE = {4{not_1_out[1]}} & FR_WE_t;  // AND_Gate and_7, 4 bits wide
  assign FR_DATA = {4{not_1_out[1]}} & FR_DATA_t;  // AND_Gate and_8, 4 bits wide
  assign ALU_OP = {4{not_1_out[1]}} & ALU_OP_t;  // AND_Gate and_9, 4 bits wide

  // Other names for the same wires on the sheet: OP_GROUP[2:0] = IR[7:5]

  // Notes on the sheet:
  //   Decode: Group
  //   Read 'decoding.txt' for signal descriptions
endmodule

module decode_system (
  input  E,
  input  [3:0] FR,
  input  [7:0] IR,
  output HLT,
  output [3:0] FR_WE,
  output [3:0] FR_DATA
);

  wire and_1_out, and_2_out, FR_WE_C, FR_WE_V, HLT_t, or_1_out, or_2_out;

  or or_1 (or_1_out, IR[0], IR[1]);
  and and_1 (and_1_out, ~HLT_t, IR[2]);  // AND_Gate
  and and_2 (and_2_out, or_1_out, ~IR[2]);  // AND_Gate
  or or_2 (or_2_out, IR[3], IR[4]);
  demux_2to1 demux_2to1_1 (.S(IR[1]), .I(and_1_out), .Y0(FR_WE_C), .Y1(FR_WE_V));
  or or_3 (HLT_t, and_2_out, or_2_out);
  and and_3 (HLT, E, HLT_t);
  assign FR_WE = {4{E}} & {FR_WE_V, FR_WE_C, 2'b00};  // AND_Gate and_4, 4 bits wide
  assign FR_DATA = {4{E}} & {{2{IR[0]}}, FR[1:0]};  // AND_Gate and_5, 4 bits wide

  // Other names for the same wires on the sheet: FR_Z = FR[0]; FR_N = FR[1]; G_SYS = E; FR_C = FR[2]; FR_V = FR[3]
endmodule

module decode_memory (
  input  E,
  input  [3:0] FR,
  input  [7:0] IR,
  output HLT,
  output MEM_RW,
  output ALU_WB,
  output [1:0] MODE,
  output [1:0] DST_SEL,
  output [2:0] SRC_SEL,
  output [3:0] ALU_OP
);

  wire ALU_WB_t, and_2_out, and_3_out, HLT_t, IS_IND, MEM_RW_t, not_1_out, not_3_out, or_1_out, SRC_REG0,
       SRC_REG1;
  wire [1:0] DST_SEL_t, MODE_t, SRC_SEL_t;

  // NoConnect on FR
  not not_1 (not_1_out, IR[4]);
  mux_2to1 mux_2to1_1 (.IN0(IR[0]), .IN1(IR[2]), .S(IR[4]), .Y(SRC_REG0));
  mux_2to1 mux_2to1_2 (.IN0(IR[1]), .IN1(IR[3]), .S(IR[4]), .Y(SRC_REG1));
  mux_2to1 mux_2to1_3 (.IN0(1'b1), .IN1(IR[0]), .S(MEM_RW_t), .Y(DST_SEL_t[0]));
  mux_2to1 mux_2to1_4 (.IN0(1'b1), .IN1(IR[1]), .S(MEM_RW_t), .Y(DST_SEL_t[1]));
  nand nand_1 (MEM_RW_t, not_1_out, IR[2]);
  and and_1 (IS_IND, IR[3], not_1_out);
  or or_1 (or_1_out, IR[4], ~MEM_RW_t);  // OR_Gate
  not not_2 (MODE_t[0], IR[4]);
  not not_3 (not_3_out, IS_IND);
  mux_2to1 mux_2to1_5 (.IN0(1'b1), .IN1(SRC_REG0), .S(or_1_out), .Y(SRC_SEL_t[0]));
  mux_2to1 mux_2to1_6 (.IN0(1'b1), .IN1(SRC_REG1), .S(or_1_out), .Y(SRC_SEL_t[1]));
  and and_2 (and_2_out, IR[0], IR[1]);
  or or_2 (HLT_t, and_2_out, and_3_out);
  and and_3 (and_3_out, IR[2], IR[3], IR[4]);
  not not_4 (ALU_WB_t, HLT_t);
  and and_4 (MODE_t[1], MODE_t[0], not_3_out);
  and and_5 (HLT, E, HLT_t);
  and and_6 (MEM_RW, E, MEM_RW_t);
  and and_7 (ALU_WB, E, ALU_WB_t);
  assign MODE = {2{E}} & MODE_t;  // AND_Gate and_8, 2 bits wide
  assign DST_SEL = {2{E}} & DST_SEL_t;  // AND_Gate and_9, 2 bits wide
  assign SRC_SEL = {3{E}} & {1'b0, SRC_SEL_t};  // AND_Gate and_10, 3 bits wide
  assign ALU_OP = {4{E}} & 4'b1000;  // AND_Gate and_11, 4 bits wide

  // Other names for the same wires on the sheet: G_MEM = E; IS_TRX = IR[4]
endmodule

module decode_arithmetic (
  input  E,
  input  [3:0] FR,
  input  [7:0] IR,
  output HLT,
  output ALU_WB,
  output [1:0] MODE,
  output [1:0] DST_SEL,
  output [2:0] SRC_SEL,
  output [3:0] ALU_OP
);

  wire ALU_WB_t, and_5_out, HLT_t, I_CMP, MAYBE_HLT, nor_1_out, xor_1_out, xor_2_out, xor_3_out;
  wire [1:1] SRC_SEL_t;
  wire [3:0] ALU_OP_t;

  // NoConnect on FR
  and and_1 (HLT_t, ~ALU_OP_t[3], MAYBE_HLT);  // AND_Gate
  and and_2 (I_CMP, IR[1], IR[2]);
  or or_1 (SRC_SEL_t[1], IR[3], IR[4]);
  and and_3 (MAYBE_HLT, IR[0], IR[1], IR[2]);
  and and_4 (ALU_OP_t[3], MAYBE_HLT, and_5_out);
  and and_5 (and_5_out, ~IR[3], IR[4]);  // AND_Gate
  xor xor_1 (xor_1_out, IR[0], I_CMP);
  xor xor_2 (xor_2_out, IR[1], I_CMP);
  xor xor_3 (xor_3_out, IR[2], I_CMP);
  nor nor_1 (nor_1_out, I_CMP, HLT_t);
  and and_6 (ALU_OP_t[0], xor_1_out, ~ALU_OP_t[3]);  // AND_Gate
  and and_7 (ALU_OP_t[1], xor_2_out, ~ALU_OP_t[3]);  // AND_Gate
  and and_8 (ALU_OP_t[2], xor_3_out, ~ALU_OP_t[3]);  // AND_Gate
  or or_2 (ALU_WB_t, nor_1_out, ALU_OP_t[3]);
  and and_9 (HLT, E, HLT_t);
  and and_10 (ALU_WB, E, ALU_WB_t);
  assign MODE = {2{E}} & IR[4:3];  // AND_Gate and_11, 2 bits wide
  assign DST_SEL = {2{E}} & 2'b00;  // AND_Gate and_12, 2 bits wide
  assign SRC_SEL = {3{E}} & {1'b0, SRC_SEL_t[1], 1'b1};  // AND_Gate and_13, 3 bits wide
  assign ALU_OP = {4{E}} & ALU_OP_t;  // AND_Gate and_14, 4 bits wide

  // Other names for the same wires on the sheet: G_ARI = E; IS_LDI = ALU_OP_t[3]; MODE_t[1:0] = IR[4:3]
endmodule

module decode_unary (
  input  E,
  input  [3:0] FR,
  input  [7:0] IR,
  output HLT,
  output ALU_WB,
  output [1:0] MODE,
  output [1:0] DST_SEL,
  output [2:0] SRC_SEL,
  output [3:0] FR_WE,
  output [3:0] FR_DATA,
  output [3:0] ALU_OP
);

  wire ALU_ROTATE, ALU_SHIFT, ALU_WB_t, and_6_out, demux_8to1_1_y0, demux_8to1_1_y1, demux_8to1_1_y2,
       demux_8to1_1_y3, demux_8to1_1_y4, demux_8to1_1_y6, demux_8to1_1_y7, HLT_t, I_DEC, I_INC, I_NOT,
       IS_HLT, N_IR3, or_4_out, xor_1_out, xor_2_out;
  wire [0:0] SRC_SEL_t;
  wire [1:0] DST_SEL_t;
  wire [2:0] ALU_OP_t;
  wire [2:2] FR_DATA_t;

  not not_1 (N_IR3, IR[3]);
  demux_8to1 demux_8to1_1 (
    .I(N_IR3), .S(IR[2:0]), .Y0(demux_8to1_1_y0), .Y1(demux_8to1_1_y1), .Y2(demux_8to1_1_y2),
    .Y3(demux_8to1_1_y3), .Y4(demux_8to1_1_y4), .Y5(I_NOT), .Y6(demux_8to1_1_y6), .Y7(demux_8to1_1_y7));
  demux_2to1 demux_2to1_1 (.S(IR[2]), .I(IR[3]), .Y0(I_INC), .Y1(I_DEC));
  or or_1 (ALU_SHIFT, demux_8to1_1_y0, demux_8to1_1_y1);
  or or_2 (IS_HLT, demux_8to1_1_y2, demux_8to1_1_y3, demux_8to1_1_y4);
  or or_3 (ALU_ROTATE, demux_8to1_1_y6, demux_8to1_1_y7);
  and and_1 (ALU_OP_t[0], IR[0], N_IR3);
  xor xor_1 (xor_1_out, IR[1], ALU_SHIFT);
  and and_2 (ALU_OP_t[1], xor_1_out, N_IR3);
  xor xor_2 (xor_2_out, IR[2], ALU_SHIFT);
  and and_3 (ALU_OP_t[2], xor_2_out, N_IR3);
  and and_4 (DST_SEL_t[0], IR[3], IR[0]);
  and and_5 (DST_SEL_t[1], IR[3], IR[1]);
  or or_4 (or_4_out, FR[2], I_INC);
  and and_6 (and_6_out, IR[3], IR[0], IR[1]);
  and and_7 (FR_DATA_t[2], or_4_out, ~ALU_SHIFT);  // AND_Gate
  or or_5 (SRC_SEL_t[0], I_DEC, I_NOT);
  or or_6 (HLT_t, IR[4], IS_HLT, and_6_out);
  not not_2 (ALU_WB_t, HLT_t);
  and and_8 (HLT, E, HLT_t);
  and and_9 (ALU_WB, E, ALU_WB_t);
  assign MODE = {2{E}} & 2'b00;  // AND_Gate and_10, 2 bits wide
  assign DST_SEL = {2{E}} & DST_SEL_t;  // AND_Gate and_11, 2 bits wide
  assign SRC_SEL = {3{E}} & {2'b11, SRC_SEL_t[0]};  // AND_Gate and_12, 3 bits wide
  assign FR_WE = {4{E}} & 4'b0000;  // AND_Gate and_13, 4 bits wide
  assign FR_DATA = {4{E}} & {FR[3], FR_DATA_t[2], FR[1:0]};  // AND_Gate and_14, 4 bits wide
  assign ALU_OP = {4{E}} & {1'b0, ALU_OP_t};  // AND_Gate and_15, 4 bits wide

  // Other names for the same wires on the sheet: G_UNY = E; FR_C = FR[2]; FR_DATA_t (some bits) = {FR[3], FR[1:0]};
  //   FR_Z = FR[0]; FR_N = FR[1]; OUT_C = FR_DATA_t[2]; FR_V = FR[3]
endmodule

module decode_jump (
  input  E,
  input  [3:0] FR,
  input  [7:0] IR,
  output HLT,
  output [1:0] MODE,
  output [1:0] PC_OP
);

  wire and_2_out, CB_BRA, demux_4to1_1_y2, demux_4to1_1_y3, HLT_t, I_BRA, I_JMP, IS_CB, IS_UCF, mux_4to1_1_y,
       nor_2_out, not_1_out, TAKE_BRANCH, xor_1_out;
  wire [1:0] PC_OP_t;

  demux_4to1 demux_4to1_1 (.I(IS_UCF), .S(IR[1:0]), .Y0(I_BRA), .Y1(I_JMP), .Y2(demux_4to1_1_y2), .Y3(demux_4to1_1_y3));
  nor nor_1 (IS_CB, IR[4], IR[3]);
  and and_1 (IS_UCF, ~IR[3], IR[4]);  // AND_Gate
  mux_4to1 mux_4to1_1 (.I0(FR[0]), .I1(FR[1]), .I2(FR[2]), .I3(FR[3]), .S(IR[1:0]), .Y(mux_4to1_1_y));
  // NoConnect on demux_4to1_1_y2
  // NoConnect on demux_4to1_1_y3
  nor nor_2 (nor_2_out, IS_CB, IS_UCF);
  and and_2 (and_2_out, IS_UCF, IR[2]);
  and and_3 (CB_BRA, IS_CB, not_1_out);
  xor xor_1 (xor_1_out, mux_4to1_1_y, IR[2]);
  not not_1 (not_1_out, xor_1_out);
  or or_1 (HLT_t, nor_2_out, and_2_out);
  or or_2 (TAKE_BRANCH, CB_BRA, I_BRA);
  and and_4 (PC_OP_t[0], ~I_JMP, TAKE_BRANCH);  // AND_Gate
  and and_5 (PC_OP_t[1], I_JMP, ~TAKE_BRANCH);  // AND_Gate
  and and_6 (HLT, E, HLT_t);
  assign MODE = {2{E}} & {1'b1, I_JMP};  // AND_Gate and_7, 2 bits wide
  assign PC_OP = {2{E}} & PC_OP_t;  // AND_Gate and_8, 2 bits wide

  // Other names for the same wires on the sheet: G_JMP = E; FR_Z = FR[0]; FR_N = FR[1]; FR_C = FR[2]; FR_V = FR[3];
  //   MODE_t[0] = I_JMP
endmodule

module multiplier_4 (
  input  [3:0] B,
  input  [3:0] A,
  output [7:0] Y,
  output Overflow
);

  wire or_1_out, or_2_out;
  wire [2:0] and_2_out;
  wire [3:0] and_5_out, and_9_out, and_13_out;
  wire [3:1] ripple_adder_4_1_y, ripple_adder_4_2_y;
  wire [3:3] ripple_adder_4_1_cout, ripple_adder_4_2_cout;

  and and_1 (Y[0], A[0], B[0]);
  and and_2 (and_2_out[0], A[1], B[0]);
  and and_3 (and_2_out[1], A[2], B[0]);
  and and_4 (and_2_out[2], A[3], B[0]);
  and and_5 (and_5_out[0], A[0], B[1]);
  and and_6 (and_5_out[1], A[1], B[1]);
  and and_7 (and_5_out[2], A[2], B[1]);
  and and_8 (and_5_out[3], A[3], B[1]);
  ripple_adder_4 ripple_adder_4_1 (
    .A(and_5_out), .B({1'b0, and_2_out}), .Cin(1'b0), .Y({ripple_adder_4_1_y, Y[1]}),
    .Cout(ripple_adder_4_1_cout[3]));
  or or_1 (or_1_out, Y[4], Y[5]);
  or or_2 (or_2_out, or_1_out, Y[6]);
  or or_3 (Overflow, Y[7], or_2_out);
  and and_9 (and_9_out[0], A[0], B[2]);
  and and_10 (and_9_out[1], A[1], B[2]);
  and and_11 (and_9_out[2], A[2], B[2]);
  and and_12 (and_9_out[3], A[3], B[2]);
  ripple_adder_4 ripple_adder_4_2 (
    .A(and_9_out), .B({ripple_adder_4_1_cout[3], ripple_adder_4_1_y}), .Cin(1'b0),
    .Y({ripple_adder_4_2_y, Y[2]}), .Cout(ripple_adder_4_2_cout[3]));
  and and_13 (and_13_out[0], A[0], B[3]);
  ripple_adder_4 ripple_adder_4_3 (
    .A(and_13_out), .B({ripple_adder_4_2_cout[3], ripple_adder_4_2_y}), .Cin(1'b0), .Y(Y[6:3]), .Cout(Y[7]));
  and and_14 (and_13_out[1], A[1], B[3]);
  and and_15 (and_13_out[2], A[2], B[3]);
  and and_16 (and_13_out[3], A[3], B[3]);
endmodule

module shifter_8 (
  input  [7:0] A,
  input  Cin,
  input  M,
  output [7:0] Y,
  output Cout
);

  mux_2to1 mux_2to1_1 (.IN0(A[2]), .IN1(A[4]), .S(M), .Y(Y[3]));
  mux_2to1 mux_2to1_2 (.IN0(A[6]), .IN1(Cin), .S(M), .Y(Y[7]));
  mux_2to1 mux_2to1_3 (.IN0(A[1]), .IN1(A[3]), .S(M), .Y(Y[2]));
  mux_2to1 mux_2to1_4 (.IN0(A[5]), .IN1(A[7]), .S(M), .Y(Y[6]));
  mux_2to1 mux_2to1_5 (.IN0(A[0]), .IN1(A[2]), .S(M), .Y(Y[1]));
  mux_2to1 mux_2to1_6 (.IN0(A[4]), .IN1(A[6]), .S(M), .Y(Y[5]));
  mux_2to1 mux_2to1_7 (.IN0(Cin), .IN1(A[1]), .S(M), .Y(Y[0]));
  mux_2to1 mux_2to1_8 (.IN0(A[3]), .IN1(A[5]), .S(M), .Y(Y[4]));
  mux_2to1 mux_2to1_9 (.IN0(A[7]), .IN1(A[0]), .S(M), .Y(Cout));
endmodule

module adder_subtractor (
  input  M,
  input  Cin,
  input  [7:0] B,
  input  [7:0] A,
  output [7:0] Y,
  output Cout,
  output Overflow
);

  wire ripple_adder_8_1_c6;
  wire [7:0] xor_8_out;

  xor xor_1 (xor_8_out[7], M, B[7]);
  xor xor_2 (xor_8_out[6], M, B[6]);
  xor xor_3 (xor_8_out[5], M, B[5]);
  xor xor_4 (xor_8_out[4], M, B[4]);
  xor xor_5 (xor_8_out[3], M, B[3]);
  xor xor_6 (xor_8_out[2], M, B[2]);
  xor xor_7 (xor_8_out[1], M, B[1]);
  xor xor_8 (xor_8_out[0], M, B[0]);
  ripple_adder_8 ripple_adder_8_1 (.A(A), .B(xor_8_out), .Cin(Cin), .Y(Y), .Cout(Cout), .C6(ripple_adder_8_1_c6));
  xor xor_9 (Overflow, Cout, ripple_adder_8_1_c6);
endmodule

module ripple_adder_8 (
  input  [7:0] A,
  input  [7:0] B,
  input  Cin,
  output [7:0] Y,
  output Cout,
  output C6
);

  wire full_adder_1_cout, full_adder_2_cout, full_adder_3_cout, full_adder_4_cout, full_adder_5_cout,
       full_adder_6_cout;

  full_adder full_adder_1 (.A(A[0]), .B(B[0]), .Cin(Cin), .Y(Y[0]), .Cout(full_adder_1_cout));
  full_adder full_adder_2 (.A(A[1]), .B(B[1]), .Cin(full_adder_1_cout), .Y(Y[1]), .Cout(full_adder_2_cout));
  full_adder full_adder_3 (.A(A[2]), .B(B[2]), .Cin(full_adder_2_cout), .Y(Y[2]), .Cout(full_adder_3_cout));
  full_adder full_adder_4 (.A(A[3]), .B(B[3]), .Cin(full_adder_3_cout), .Y(Y[3]), .Cout(full_adder_4_cout));
  full_adder full_adder_5 (.A(A[4]), .B(B[4]), .Cin(full_adder_4_cout), .Y(Y[4]), .Cout(full_adder_5_cout));
  full_adder full_adder_6 (.A(A[5]), .B(B[5]), .Cin(full_adder_5_cout), .Y(Y[5]), .Cout(full_adder_6_cout));
  full_adder full_adder_7 (.A(A[6]), .B(B[6]), .Cin(full_adder_6_cout), .Y(Y[6]), .Cout(C6));
  full_adder full_adder_8 (.A(A[7]), .B(B[7]), .Cin(C6), .Y(Y[7]), .Cout(Cout));
endmodule

module ripple_adder_4 (
  input  [3:0] A,
  input  [3:0] B,
  input  Cin,
  output [3:0] Y,
  output Cout
);

  wire full_adder_1_cout, full_adder_2_cout, full_adder_3_cout;

  full_adder full_adder_1 (.A(A[0]), .B(B[0]), .Cin(Cin), .Y(Y[0]), .Cout(full_adder_1_cout));
  full_adder full_adder_2 (.A(A[1]), .B(B[1]), .Cin(full_adder_1_cout), .Y(Y[1]), .Cout(full_adder_2_cout));
  full_adder full_adder_3 (.A(A[2]), .B(B[2]), .Cin(full_adder_2_cout), .Y(Y[2]), .Cout(full_adder_3_cout));
  full_adder full_adder_4 (.A(A[3]), .B(B[3]), .Cin(full_adder_3_cout), .Y(Y[3]), .Cout(Cout));
endmodule

module full_adder (
  input  A,
  input  B,
  input  Cin,
  output Y,
  output Cout
);

  wire and_1_out, and_2_out, xor_1_out;

  xor xor_1 (xor_1_out, A, B);
  and and_1 (and_1_out, xor_1_out, Cin);
  and and_2 (and_2_out, A, B);
  xor xor_2 (Y, xor_1_out, Cin);
  or or_1 (Cout, and_1_out, and_2_out);
endmodule

module d_flipflop (
  input  D,
  input  CLK,
  input  RST,
  output Q,
  output NQ
);

  D_Flip_Flop d_ff_1 (.D(D), .clk(CLK), .Q(Q), .Qn(NQ), .reset(RST));  // open: preset

  // Notes on the sheet:
  //   Rising edge D-FlipFlop
  //   I'm using the default d-flipflop 'cause it's impossible to simulate the correct behaviour with the 'd_latch' module. See 'd_latch' module
endmodule

module d_latch (
  input  D,
  input  CLK,
  input  RST,
  output Q,
  output NQ
);

  wire buffer_1_out, buffer_2_out, buffer_3_out, nand_1_out, nand_2_out, nor_1_out;

  nor nor_1 (nor_1_out, D, RST);
  nand nand_1 (nand_1_out, D, CLK);
  nand nand_2 (nand_2_out, CLK, nor_1_out);
  buf buffer_1 (buffer_1_out, buffer_2_out);
  buf buffer_2 (buffer_2_out, buffer_3_out);
  nand nand_3 (Q, NQ, nand_1_out);
  nand nand_4 (NQ, nand_2_out, buffer_1_out);
  buf buffer_3 (buffer_3_out, Q);

  // Notes on the sheet:
  //   Logisim is BUGGY, So I can't use this implementation
  //   if you are reading this, I've lost my mind and gone insane :3
endmodule

module mux_2to1 (
  input  S,
  input  IN0,
  input  IN1,
  output Y
);

  wire nand_1_out, nand_3_out, not_1_out;

  not not_1 (not_1_out, S);
  nand nand_1 (nand_1_out, not_1_out, IN0);
  nand nand_2 (Y, nand_1_out, nand_3_out);
  nand nand_3 (nand_3_out, IN1, S);
endmodule

module mux_2to1_2 (
  input  S,
  input  [1:0] IN0,
  input  [1:0] IN1,
  output [1:0] Y
);

  mux_2to1 mux_2to1_1 (.IN0(IN0[0]), .IN1(IN1[0]), .S(S), .Y(Y[0]));
  mux_2to1 mux_2to1_2 (.IN0(IN0[1]), .IN1(IN1[1]), .S(S), .Y(Y[1]));

  // Other names for the same wires on the sheet: IN0_0 = IN0[0]; IN0_1 = IN0[1]; IN1_0 = IN1[0]; IN1_1 = IN1[1]
endmodule

module mux_2to1_4 (
  input  S,
  input  [3:0] IN0,
  input  [3:0] IN1,
  output [3:0] Y
);

  mux_2to1 mux_2to1_1 (.IN0(IN0[0]), .IN1(IN1[0]), .S(S), .Y(Y[0]));
  mux_2to1 mux_2to1_2 (.IN0(IN0[1]), .IN1(IN1[1]), .S(S), .Y(Y[1]));
  mux_2to1 mux_2to1_3 (.IN0(IN0[2]), .IN1(IN1[2]), .S(S), .Y(Y[2]));
  mux_2to1 mux_2to1_4 (.IN0(IN0[3]), .IN1(IN1[3]), .S(S), .Y(Y[3]));
endmodule

module mux_2to1_8 (
  input  S,
  input  [7:0] IN0,
  input  [7:0] IN1,
  output [7:0] Y
);

  mux_2to1_4 mux_2to1_4_1 (.S(S), .IN0(IN0[3:0]), .IN1(IN1[3:0]), .Y(Y[3:0]));
  mux_2to1_4 mux_2to1_4_2 (.S(S), .IN0(IN0[7:4]), .IN1(IN1[7:4]), .Y(Y[7:4]));
endmodule

module mux_4to1 (
  input  I0,
  input  I1,
  input  I2,
  input  I3,
  input  [1:0] S,
  output Y
);

  wire mux_2to1_1_y, mux_2to1_3_y;

  mux_2to1 mux_2to1_1 (.IN0(I0), .IN1(I1), .S(S[0]), .Y(mux_2to1_1_y));
  mux_2to1 mux_2to1_2 (.IN0(mux_2to1_1_y), .IN1(mux_2to1_3_y), .S(S[1]), .Y(Y));
  mux_2to1 mux_2to1_3 (.IN0(I2), .IN1(I3), .S(S[0]), .Y(mux_2to1_3_y));
endmodule

module mux_4to1_4 (
  input  [1:0] S,
  input  [3:0] IN0,
  input  [3:0] IN1,
  input  [3:0] IN2,
  input  [3:0] IN3,
  output [3:0] Y
);

  mux_4to1 mux_4to1_1 (.I0(IN0[0]), .I1(IN1[0]), .I2(IN2[0]), .I3(IN3[0]), .S(S), .Y(Y[0]));
  mux_4to1 mux_4to1_2 (.I0(IN0[1]), .I1(IN1[1]), .I2(IN2[1]), .I3(IN3[1]), .S(S), .Y(Y[1]));
  mux_4to1 mux_4to1_3 (.I0(IN0[2]), .I1(IN1[2]), .I2(IN2[2]), .I3(IN3[2]), .S(S), .Y(Y[2]));
  mux_4to1 mux_4to1_4 (.I0(IN0[3]), .I1(IN1[3]), .I2(IN2[3]), .I3(IN3[3]), .S(S), .Y(Y[3]));
endmodule

module mux_4to1_8 (
  input  [7:0] I0,
  input  [7:0] I1,
  input  [7:0] I2,
  input  [7:0] I3,
  input  [1:0] S,
  output [7:0] Y
);

  mux_4to1_4 mux_4to1_4_1 (.S(S), .IN0(I0[3:0]), .IN1(I1[3:0]), .IN2(I2[3:0]), .IN3(I3[3:0]), .Y(Y[3:0]));
  mux_4to1_4 mux_4to1_4_2 (.S(S), .IN0(I0[7:4]), .IN1(I1[7:4]), .IN2(I2[7:4]), .IN3(I3[7:4]), .Y(Y[7:4]));

  // Other names for the same wires on the sheet: I0_L[3:0] = I0[3:0]; I0_H[3:0] = I0[7:4]; I1_L[3:0] = I1[3:0];
  //   I1_H[3:0] = I1[7:4]; I2_L[3:0] = I2[3:0]; I2_H[3:0] = I2[7:4]; I3_L[3:0] = I3[3:0]; I3_H[3:0] = I3[7:4];
  //   SEL[1:0] = S; Y_L[3:0] = Y[3:0]; Y_H[3:0] = Y[7:4]
endmodule

module mux_4to1_16 (
  input  [15:0] I0,
  input  [15:0] I1,
  input  [15:0] I2,
  input  [15:0] I3,
  input  [1:0] S,
  output [15:0] Y
);

  mux_4to1_8 mux_4to1_8_1 (.I0(I0[7:0]), .I1(I1[7:0]), .I2(I2[7:0]), .I3(I3[7:0]), .S(S), .Y(Y[7:0]));
  mux_4to1_8 mux_4to1_8_2 (.I0(I0[15:8]), .I1(I1[15:8]), .I2(I2[15:8]), .I3(I3[15:8]), .S(S), .Y(Y[15:8]));

  // Other names for the same wires on the sheet: I0_L[7:0] = I0[7:0]; I0_H[7:0] = I0[15:8]; I1_L[7:0] = I1[7:0];
  //   I1_H[7:0] = I1[15:8]; I2_L[7:0] = I2[7:0]; I2_H[7:0] = I2[15:8]; I3_L[7:0] = I3[7:0]; I3_H[7:0] = I3[15:8];
  //   SEL[1:0] = S; Y_L[7:0] = Y[7:0]; Y_H[7:0] = Y[15:8]
endmodule

module mux_8to1 (
  input  [2:0] S,
  input  I0,
  input  I1,
  input  I2,
  input  I3,
  input  I4,
  input  I5,
  input  I6,
  input  I7,
  output out_10
);

  wire mux_4to1_1_y, mux_4to1_2_y;

  mux_4to1 mux_4to1_1 (.I0(I0), .I1(I1), .I2(I2), .I3(I3), .S(S[1:0]), .Y(mux_4to1_1_y));
  mux_2to1 mux_2to1_1 (.IN0(mux_4to1_1_y), .IN1(mux_4to1_2_y), .S(S[2]), .Y(out_10));
  mux_4to1 mux_4to1_2 (.I0(I4), .I1(I5), .I2(I6), .I3(I7), .S(S[1:0]), .Y(mux_4to1_2_y));
endmodule

module mux_8to1_8 (
  input  [7:0] IN7,
  input  [7:0] IN6,
  input  [7:0] IN5,
  input  [7:0] IN4,
  input  [7:0] IN3,
  input  [7:0] IN2,
  input  [7:0] IN1,
  input  [7:0] IN0,
  input  [2:0] S,
  output [7:0] out_10
);

  wire [3:0] mux_4to1_4_1_y, mux_4to1_4_2_y, mux_4to1_4_3_y, mux_4to1_4_4_y;

  mux_4to1_4 mux_4to1_4_1 (
    .S(S[1:0]), .IN0(IN0[3:0]), .IN1(IN1[3:0]), .IN2(IN2[3:0]), .IN3(IN3[3:0]), .Y(mux_4to1_4_1_y));
  mux_4to1_4 mux_4to1_4_2 (
    .S(S[1:0]), .IN0(IN4[3:0]), .IN1(IN5[3:0]), .IN2(IN6[3:0]), .IN3(IN7[3:0]), .Y(mux_4to1_4_2_y));
  mux_4to1_4 mux_4to1_4_3 (
    .S(S[1:0]), .IN0(IN0[7:4]), .IN1(IN1[7:4]), .IN2(IN2[7:4]), .IN3(IN3[7:4]), .Y(mux_4to1_4_3_y));
  mux_4to1_4 mux_4to1_4_4 (
    .S(S[1:0]), .IN0(IN4[7:4]), .IN1(IN5[7:4]), .IN2(IN6[7:4]), .IN3(IN7[7:4]), .Y(mux_4to1_4_4_y));
  mux_2to1_4 mux_2to1_4_1 (.S(S[2]), .IN0(mux_4to1_4_1_y), .IN1(mux_4to1_4_2_y), .Y(out_10[3:0]));
  mux_2to1_4 mux_2to1_4_2 (.S(S[2]), .IN0(mux_4to1_4_3_y), .IN1(mux_4to1_4_4_y), .Y(out_10[7:4]));
endmodule

module demux_2to1 (
  input  S,
  input  I,
  output Y0,
  output Y1
);

  wire not_1_out;

  not not_1 (not_1_out, S);
  and and_1 (Y0, not_1_out, I);
  and and_2 (Y1, S, I);
endmodule

module demux_2to1_8 (
  input  [7:0] I,
  input  S,
  output [7:0] Y0,
  output [7:0] Y1
);

  demux_2to1 demux_2to1_1 (.S(S), .I(I[0]), .Y0(Y0[0]), .Y1(Y1[0]));
  demux_2to1 demux_2to1_2 (.S(S), .I(I[1]), .Y0(Y0[1]), .Y1(Y1[1]));
  demux_2to1 demux_2to1_3 (.S(S), .I(I[2]), .Y0(Y0[2]), .Y1(Y1[2]));
  demux_2to1 demux_2to1_4 (.S(S), .I(I[3]), .Y0(Y0[3]), .Y1(Y1[3]));
  demux_2to1 demux_2to1_5 (.S(S), .I(I[4]), .Y0(Y0[4]), .Y1(Y1[4]));
  demux_2to1 demux_2to1_6 (.S(S), .I(I[5]), .Y0(Y0[5]), .Y1(Y1[5]));
  demux_2to1 demux_2to1_7 (.S(S), .I(I[6]), .Y0(Y0[6]), .Y1(Y1[6]));
  demux_2to1 demux_2to1_8 (.S(S), .I(I[7]), .Y0(Y0[7]), .Y1(Y1[7]));

  // Other names for the same wires on the sheet: I_0 = I[0]; I_1 = I[1]; I_2 = I[2]; I_3 = I[3]; I_4 = I[4];
  //   I_5 = I[5]; I_6 = I[6]; I_7 = I[7]; SEL = S; Y0_0 = Y0[0]; Y0_1 = Y0[1]; Y0_2 = Y0[2]; Y0_3 = Y0[3];
  //   Y0_4 = Y0[4]; Y0_5 = Y0[5]; Y0_6 = Y0[6]; Y0_7 = Y0[7]; Y1_0 = Y1[0]; Y1_1 = Y1[1]; Y1_2 = Y1[2]; Y1_3 = Y1[3];
  //   Y1_4 = Y1[4]; Y1_5 = Y1[5]; Y1_6 = Y1[6]; Y1_7 = Y1[7]
endmodule

module demux_4to1 (
  input  I,
  input  [1:0] S,
  output Y0,
  output Y1,
  output Y2,
  output Y3
);

  wire demux_2to1_1_y0, demux_2to1_1_y1;

  demux_2to1 demux_2to1_1 (.S(S[1]), .I(I), .Y0(demux_2to1_1_y0), .Y1(demux_2to1_1_y1));
  demux_2to1 demux_2to1_2 (.S(S[0]), .I(demux_2to1_1_y0), .Y0(Y0), .Y1(Y1));
  demux_2to1 demux_2to1_3 (.S(S[0]), .I(demux_2to1_1_y1), .Y0(Y2), .Y1(Y3));
endmodule

module demux_8to1 (
  input  I,
  input  [2:0] S,
  output Y0,
  output Y1,
  output Y2,
  output Y3,
  output Y4,
  output Y5,
  output Y6,
  output Y7
);

  wire demux_2to1_1_y0, demux_2to1_1_y1;

  demux_2to1 demux_2to1_1 (.S(S[2]), .I(I), .Y0(demux_2to1_1_y0), .Y1(demux_2to1_1_y1));
  demux_4to1 demux_4to1_1 (.I(demux_2to1_1_y0), .S(S[1:0]), .Y0(Y0), .Y1(Y1), .Y2(Y2), .Y3(Y3));
  demux_4to1 demux_4to1_2 (.I(demux_2to1_1_y1), .S(S[1:0]), .Y0(Y4), .Y1(Y5), .Y2(Y6), .Y3(Y7));
endmodule
